# Fritzing sketch arduino 2 (saved by Fritzing 0.9.3b)
breadboards: 1

parts:
  U1 = GAS_SENSOR [package=mq-3]
  R1 = Photocell (LDR) [package=THT]
  U2 = MLX90614 [package=to-39]
  Raspberry_Pi_1 = Raspberry Pi 3 [part_number=RPI-3-V1.2]  # not connected
  부품1 = Arduino Uno (Rev3)
  R2 = Resistor [tolerance=±5% resistance=220 package=THT]

nets:
  N1: U1.B1, R1.pin_0, U2.SCL_VZ, 부품1.5V
  N2: U1.A1, U2.PWM_SDA, 부품1.GND, R2.Pin_1
  N3: U1.H1, 부품1.A1
  N4: R1.pin_1, 부품1.A0, R2.Pin_0
  N5: U2.VDD, 부품1.D10_PWM/SS
